# Fritzing sketch stib-iot (saved by Fritzing 0.9.3b)
breadboards: 1

parts:
  U1 = NodeMCU V1.0
  VCC1 = 4 x AAA Battery Mount
  S1 = Momentary Switch [package=ksa_sealed_tac_switch]
  S2 = Momentary Switch [package=ksa_sealed_tac_switch]
  R1 = Resistor [tolerance=±5% resistance=10k package="1206 [SMD]"]
  R2 = Resistor [tolerance=±5% resistance=10k package="1206 [SMD]"]
  S3 = Toggle Switch [package=THT]
  Composant1 = LCD1602-I2C

nets:
  N1: U1.D1, Composant1.SCL
  N2: U1.D2, Composant1.SDA
  N3: U1.D4, S2.3
  GND: U1.GND, S1.2, S2.2, R1.Pin_1, R2.Pin_1, S3.L2, Composant1.GND
  N4: U1.D5, S1.3
  VIN: U1.Vin, VCC1.+, Composant1.VCC
  N5: VCC1.-, S3.L1
  N6: S1.4, R1.Pin_0
  N7: S2.4, R2.Pin_0

custom parts:
  NodeMCU V1.0: ESP9266 based NodeMCU
  LCD1602-I2C: A standard character display, usually with 2x16 characters. Comes in many colors with LCM1602 IIC attached.

// code stored in the sketch: PassingTime.h.ino
class PassingTime{
  String line;
  String destination;
  String expectedTime;

  public:
    PassingTime(String line, String destination, String expectedTime) : 
      line(line),
      destination(destination),
      expectedTime(expectedTime)
    {      
    }

    String getDisplay(){
      return line + " " + destination.substring(0, 7) + " " + expectedTime.substring(11, 16);
    }

    String getRemainingTime(){
      return expectedTime.substring(14, 16);
    }
};


class PassingTimeResponse{
  public:
    int numberOfResponses = 0;
    PassingTime **passingTimes;
  
    PassingTimeResponse(PassingTime **items, int arraySize){
      passingTimes = items;
      numberOfResponses = arraySize;    
    }
};

// code stored in the sketch: StibIotHttpClient2.ino
/*
    HTTP over TLS (HTTPS) example sketch

    This example demonstrates how to use
    WiFiClientSecure class to access HTTPS API.
    We fetch and display the status of
    esp8266/Arduino project continuous integration
    build.

    Limitations:
      only RSA certificates
      no support of Perfect Forward Secrecy (PFS)
      TLSv1.2 is supported since version 2.4.0-rc1

    Created by Ivan Grokhotkov, 2015.
    This example is in public domain.
*/
#include "PassingTime.h"
#include <ESP8266WiFi.h>

#include <ESP8266HTTPClient.h>
#include <WiFiClientSecureBearSSL.h>
#include "ArduinoJson.h"
#include <ArduinoSort.h>

#ifndef STASSID
#define STASSID "Kev Network"
#define STAPSK  "rA3E4XuG1w3y"
#endif
#include <Wire.h>  // This library is already built in to the Arduino IDE
#include <LiquidCrystal_I2C.h> //This library you can add via Include Library > Manage Library > 

const String APP_NAME = "Stib IOT - " __FILE__;
const String APP_VERSION = "v0.1-" __DATE__ " " __TIME__;

LiquidCrystal_I2C lcd(0x27, 16, 2);

const char* ssid = STASSID;
const char* password = STAPSK;

const String host = "https://opendata-api.stib-mivb.be";
const int httpsPort = 443;
const String endPointToken = "/token";
const String endPointPassingTime = host + "/OperationMonitoring/3.0/PassingTimeByPoint";
const String ARSENAL_TRAM_ROGIER = "5267";
const String ARSENAL_34_AUDERGHEM = "1715";

// Use web browser to view and copy
// SHA1 fingerprint of the certificate
const char fingerprint[] PROGMEM = "5f 88 a4 69 77 f0 69 00 5d 6f 71 19 3d e2 2e 20 44 48 f0 b3";

const char* token = "Bearer 1684394273e8a9bab2cf0f84ac6daec8";
DynamicJsonBuffer jsonBuffer(512);
PassingTime *passingTimes[10];
const char * headerKeys[] = {"date"};
const size_t numberOfHeaders = 1;

#define BLUE_BUTTON D5
#define RED_BUTTON D4

void setup() {
  Serial.begin(115200);
  Serial.println();
  Serial.println(APP_NAME);
  Serial.println(APP_VERSION);
  Serial.print("connecting to ");
  Serial.println(ssid);
  pinMode(BLUE_BUTTON, INPUT);
  pinMode(RED_BUTTON, INPUT); 
  
  lcd.init();   // initializing the LCD
  lcd.backlight(); // Enable or Turn On the backlight 

  if(!connectToWifi()){
    Serial.println("Fail to connect. Reset micro controller.");
    setup();
  }
}

bool connectToWifi(){
  lcd.print("Connecting WiFi ");
  WiFi.mode(WIFI_STA);
  WiFi.begin(ssid, password);
  lcd.setCursor(0,1);
  int count = 0;
  while (WiFi.status() != WL_CONNECTED) {
    delay(500);
    lcd.print(".");
    Serial.print(".");
    count++;
    if(count>10){
      return false;
    }
  }
  lcd.clear();
  Serial.println("");
  lcd.print("WiFi connected");
  Serial.println("WiFi connected");
  Serial.println("IP address: ");
  Serial.println(WiFi.localIP()); 
  return true;
}

void displayPassingTimeOnLcd(PassingTimeResponse* passingTimeResponse){
  lcd.clear();
  lcd.print(passingTimeResponse->passingTimes[0]->getDisplay());
  lcd.setCursor(0,1);
  lcd.print(passingTimeResponse->passingTimes[1]->getDisplay());
}

PassingTimeResponse* getPassingTime(String stopId){
  String url = endPointPassingTime + "/" + stopId;
  Serial.printf("[HTTPS] begin %s \n", url.c_str());
  
  std::unique_ptr<BearSSL::WiFiClientSecure>client(new BearSSL::WiFiClientSecure);
  client->setFingerprint(fingerprint);
  HTTPClient http;
  lcd.clear();
  lcd.print("Get passing time");
  if (http.begin(*client, url)) {  // HTTP
      http.addHeader("Accept", "application/json");
      http.addHeader("Authorization", token);
      Serial.print("[HTTPS] GET...\n");
      http.collectHeaders(headerKeys, numberOfHeaders);
      // start connection and send HTTP header
      int httpCode = http.GET();
      PassingTimeResponse * passingTimeResponse;
      if (httpCode > 0) {
        // HTTP header has been send and Server response header has been handled
        Serial.printf("[HTTPS] GET... code: %d\n", httpCode);
        
        // file found at server
        if (httpCode == HTTP_CODE_OK || httpCode == HTTP_CODE_MOVED_PERMANENTLY) {
          String payload = http.getString();
          int j = 0;
          Serial.println(http.header(j));
          JsonObject& root = jsonBuffer.parseObject(payload);
          if(!root.success()){
            Serial.println("Fail to parse object");  
            return 0;
          }
          JsonArray& passingTimesArr = root["points"][0]["passingTimes"];
          if(!passingTimesArr.success()){
            Serial.println("Fail to parse passingTimes");  
            return 0;
          }
          passingTimeResponse = getPassingTimeResponse(passingTimesArr);
          
          Serial.println("Response:");
          for(int k =0; k<passingTimeResponse->numberOfResponses ; k++){
            Serial.println(passingTimeResponse->passingTimes[k]->getDisplay());
          }
          Serial.println("---------------");
        }
      } else {
        Serial.printf("[HTTPS] GET... failed, error: %s\n", http.errorToString(httpCode).c_str());
      }

      http.end();
      return passingTimeResponse;
  } else {
    Serial.printf("[HTTPS] Unable to connect\n");
  }
  return 0;
}

PassingTimeResponse* getPassingTimeResponse(JsonArray& passingTimesArr){
  int i = 0;
  static PassingTime *passingTimes[10];
  for (JsonObject& val : passingTimesArr){
    passingTimes[i] = new PassingTime(val["lineId"].as<String>(), val["destination"]["fr"].as<String>(), val["expectedArrivalTime"].as<String>());
    Serial.println(passingTimes[i]->getDisplay());
    i++;
  }
  sortArray(passingTimes, i, sortPassingTimes);
  
  return new PassingTimeResponse(passingTimes, i);
}


bool sortPassingTimes(PassingTime *a, PassingTime *b){
  return a->getRemainingTime() > b->getRemainingTime();
}
int redState = 0;
int blueState = 0;
String stopIdToFetch;

void loop() {
  redState=digitalRead(RED_BUTTON);
  blueState=digitalRead(BLUE_BUTTON);
  if(redState == HIGH || blueState == HIGH ){
    if(redState == HIGH ){
      Serial.println("Red was pushed");
      stopIdToFetch = ARSENAL_TRAM_ROGIER;
    } else {
      Serial.println("Blue was pushed");
      stopIdToFetch = ARSENAL_34_AUDERGHEM;
    }
    PassingTimeResponse* passingTimeResponse = getPassingTime(stopIdToFetch);
    if( passingTimeResponse != 0 ){
      displayPassingTimeOnLcd(passingTimeResponse); 
    }else{
      lcd.clear();
      lcd.print("Error");
    }
  }
  delay(200);
}
